// Logisim project CPU.circ as structural Verilog: 11 circuits, main circuit CPU
module Program_Counter (
  input  JUMP,
  input  [7:0] ADDR1,
  input  LOAD,
  input  CLK,
  input  CLEAR,
  output [7:0] OUT
);

  wire not_2_out, not_3_out, or_1_out;
  wire [8:0] _9x_2_out, _9x_3_out, _9x_out, adder_1_out, not_1_out, Register_q;

  assign not_1_out = ~{9{JUMP}};  // NOT_Gate not_1, 9 bits wide
  assign _9x_out = {9{JUMP}} & {1'b0, ADDR1};  // AND_Gate _9x, 9 bits wide
  not not_2 (not_2_out, JUMP);
  assign _9x_2_out = adder_1_out & not_1_out;  // AND_Gate _9x_2, 9 bits wide
  assign _9x_3_out = _9x_2_out | _9x_out;  // OR_Gate _9x_3, 9 bits wide
  not not_3 (not_3_out, not_2_out);
  Register #(.width(9)) Register (.D({1'b0, _9x_3_out[7:0]}), .en(1'b1), .Q(Register_q), .clk(or_1_out), .clr(CLEAR));
  or or_1 (or_1_out, not_3_out, CLK);
  Adder #(.width(9)) adder_1 (.a(9'h1), .b(Register_q), .out(adder_1_out));  // open: cin, cout
  assign OUT = Register_q[7:0] & {8{LOAD}};  // AND_Gate _8x, 8 bits wide
endmodule

module CPU (
  input  in_1,
  input  PROGRAM_MODE,
  input  RESUME
);

  wire alu_1__0, and_1_out, and_2_out, clock_1__0, clock_1__1, clock_1__2, clock_1__3, clock_1__4, d_ff_2_q,
       d_ff_4_q, decoder_1_add, decoder_1_cla, decoder_1_getmem, decoder_1_hrs, decoder_1_jmp, decoder_1_sto,
       decoder_1_sub, decoder_1_tac, or_1_out, or_2_out, or_3_out, or_4_out, or_5_out, or_6_out, or_7_out,
       or_8_out, s_r_ff_1_q, s_r_ff_2_q, s_r_ff_2_qn, xor_1_out;
  wire [7:0] _8x_2_out, _8x_3_out, _8x_out, and_3_out, and_7_out, instruction_register_1_address,
       instruction_register_1_instruction, program_counter_1_out, register_3_q, xor_2_out;
  wire [7:7] and_6_out, d_ff_3_q, decoder_1_out, decoder_1_sft;
  wire [15:0] _8x_4_out, _16x_out, ACCUMULATOR_q, alu_1_out, and_4_out, and_5_out,
       nv_mem_loader_addresser_4_kb_256_words_1_dataout, ram_1_data, register_1_q, register_2_q;
  wire [15:15] d_ff_1_q, decoder_1_inp;

  or or_1 (or_1_out, decoder_1_hrs, PROGRAM_MODE);
  and and_1 (and_1_out, and_2_out, s_r_ff_1_q);
  and and_2 (and_2_out, s_r_ff_2_qn, clock_1__3);
  Register #(.width(16)) ACCUMULATOR (.D(alu_1_out), .Q(ACCUMULATOR_q), .clk(and_1_out), .clr(or_1_out));  // open: en
  S_R_Flip_Flop #(.trigger("high")) s_r_ff_1 (
    .Q(s_r_ff_1_q), .preset(or_2_out), .reset(clock_1__4));  // open: S, clk, R, Qn, en
  or or_2 (or_2_out, decoder_1_cla, decoder_1_sub, decoder_1_sft[7], decoder_1_add);
  Clock clock_1 (
    ._4(clock_1__4), ._3(clock_1__3), ._2(clock_1__2), ._1(clock_1__1), ._0(clock_1__0),
    .PROGMOD(PROGRAM_MODE), .HALT(decoder_1_hrs), .RESUME(RESUME));
  ALU alu_1 (
    .SUB(decoder_1_sub), .ADD(decoder_1_add), .OPERAND(ram_1_data), .ACCUMULATOR(ACCUMULATOR_q),
    .OUT(alu_1_out), .SETOP(clock_1__2), .TAC(decoder_1_tac), ._0(alu_1__0), .CLA(decoder_1_cla),
    .SFT(decoder_1_sft[7]));
  D_Flip_Flop d_ff_1 (.Q(d_ff_1_q[15]), .preset(clock_1__2), .reset(clock_1__4));  // open: clk, D, Qn, en
  or or_3 (or_3_out, clock_1__1, clock_1__0);
  Decoder decoder_1 (
    .INSTRUCTION(instruction_register_1_instruction), .ADD(decoder_1_add), .SUB(decoder_1_sub),
    .JMP(decoder_1_jmp), .TAC(decoder_1_tac), .STO(decoder_1_sto), .CLA(decoder_1_cla), .HRS(decoder_1_hrs),
    .OUT(decoder_1_out[7]), .INP(decoder_1_inp[15]), .INSTOUT(clock_1__2), .GETMEM(decoder_1_getmem),
    .SFT(decoder_1_sft[7]));
  S_R_Flip_Flop #(.trigger("high")) s_r_ff_2 (
    .Q(s_r_ff_2_q), .Qn(s_r_ff_2_qn), .preset(or_4_out), .reset(clock_1__0));  // open: S, clk, R, en
  or or_4 (or_4_out, alu_1__0, decoder_1_jmp);
  ExactlyOne xor_1 (.out(xor_1_out), .in0(s_r_ff_2_q), .in1(s_r_ff_2_q), .in4(clock_1__4));
  or or_5 (or_5_out, clock_1__2, clock_1__1, clock_1__0);
  Instruction_Register instruction_register_1 (
    .MEM(ram_1_data), .CLK(clock_1__1), .ADDRESS(instruction_register_1_address),
    .INSTRUCTION(instruction_register_1_instruction), .DOOUT(clock_1__2), .INSTOUT(1'b1));
  D_Flip_Flop d_ff_2 (.Q(d_ff_2_q), .preset(decoder_1_inp[15]), .reset(clock_1__4));  // open: clk, D, Qn, en
  Program_Counter program_counter_1 (
    .JUMP(or_4_out), .CLEAR(decoder_1_hrs), .OUT(program_counter_1_out), .LOAD(or_3_out), .CLK(xor_1_out),
    .ADDR1(instruction_register_1_address));
  D_Flip_Flop d_ff_3 (.Q(d_ff_3_q[7]), .preset(decoder_1_getmem), .reset(clock_1__0));  // open: clk, D, Qn, en
  assign and_3_out = instruction_register_1_address & {8{d_ff_3_q[7]}};  // AND_Gate and_3, 8 bits wide
  ExactlyOne _8x[7:0] (.out(_8x_out), .in0(xor_2_out), .in3({8{decoder_1_out[7]}}), .in4({8{decoder_1_out[7]}}));
  or or_6 (or_6_out, d_ff_2_q, decoder_1_inp[15]);
  ExactlyOne xor_2[7:0] (.out(xor_2_out), .in0(_8x_2_out), .in1({8{decoder_1_sft[7]}}), .in2({8{decoder_1_sft[7]}}));
  assign _8x_2_out = instruction_register_1_address | program_counter_1_out;  // OR_Gate _8x_2, 8 bits wide
  Register #(.width(16), .trigger("high")) register_1 (
    .D(and_5_out), .Q(register_1_q), .clk(or_6_out), .clr(clock_1__4));  // open: en
  or or_7 (or_7_out, or_5_out, decoder_1_hrs);
  Register #(.width(16), .trigger("high")) register_2 (
    .D(ram_1_data), .Q(register_2_q), .clk(decoder_1_out[7]));  // open: en, clr
  assign _8x_3_out = and_7_out | _8x_out | and_3_out;  // OR_Gate _8x_3, 8 bits wide
  ExactlyOne _16x[15:0] (
    .out(_16x_out), .in1(ACCUMULATOR_q), .in3({16{decoder_1_inp[15]}}), .in4({16{decoder_1_inp[15]}}));
  assign _8x_4_out = _16x_out | and_4_out;  // OR_Gate _8x_4, 16 bits wide
  assign and_4_out = register_1_q & {16{d_ff_1_q[15]}};  // AND_Gate and_4, 16 bits wide
  NV_Mem_Loader_Addresser___4_KB___256_words nv_mem_loader_addresser_4_kb_256_words_1 (
    .MODE(in_1), .NEXT(decoder_1_inp[15]), .RESETINDEX(1'b0),
    .DATAOUT(nv_mem_loader_addresser_4_kb_256_words_1_dataout));
  assign and_5_out = {16{decoder_1_inp[15]}} & nv_mem_loader_addresser_4_kb_256_words_1_dataout;  // AND_Gate and_5, 16 bits wide
  Hex_Digit_Display hex_digit_display_1 (.value(register_2_q[11:8]));  // open: dp
  Hex_Digit_Display hex_digit_display_2 (.value(register_2_q[15:12]));  // open: dp
  RAM #(.dataWidth(16), .bus("separate")) ram_1 (
    .addr(_8x_3_out), .din(_8x_4_out), .data(ram_1_data), .str(and_6_out[7]), .clk(and_6_out[7]),
    .ld(or_7_out));  // open: sel, clr
  Hex_Digit_Display hex_digit_display_3 (.value(register_2_q[3:0]));  // open: dp
  Hex_Digit_Display hex_digit_display_4 (.value(register_2_q[7:4]));  // open: dp
  Register #(.trigger("high")) register_3 (.D(and_3_out), .Q(register_3_q), .clk(decoder_1_inp[15]));  // open: en, clr
  and and_6 (and_6_out[7], d_ff_4_q, clock_1__3);
  D_Flip_Flop d_ff_4 (.Q(d_ff_4_q), .preset(or_8_out), .reset(clock_1__4));  // open: clk, D, Qn, en
  or or_8 (or_8_out, decoder_1_inp[15], decoder_1_sto);
  assign and_7_out = register_3_q & {8{and_6_out[7]}};  // AND_Gate and_7, 8 bits wide
endmodule

module ALU (
  input  SUB,
  input  [15:0] OPERAND,
  input  ADD,
  input  [15:0] ACCUMULATOR,
  input  SETOP,
  input  TAC,
  input  CLA,
  input  SFT,
  output [15:0] OUT,
  output _0
);

  wire not_1_out;
  wire [15:0] _16x_2_out, _16x_3_out, _16x_4_out, _16x_5_out, _16x_6_out, _16x_7_out, _16x_8_out, _16x_9_out,
       _16x_out, adder_1_out, not_7_out, register_1_q, shifter_1_out, shifter_2_out, x16_out;
  wire [15:15] not_2_out, not_3_out, not_4_out, not_5_out, not_6_out;

  not not_1 (not_1_out, SFT);
  not not_2 (not_2_out[15], SUB);
  not not_3 (not_3_out[15], ADD);
  Register #(.width(16), .trigger("high")) register_1 (
    .D(OPERAND), .en(not_1_out), .Q(register_1_q), .clk(SETOP));  // open: clr
  not not_4 (not_4_out[15], TAC);
  not not_5 (not_5_out[15], CLA);
  not not_6 (not_6_out[15], SFT);
  ExactlyOne _16x[15:0] (.out(_16x_out), .in0({16{not_2_out[15]}}), .in1({16{not_2_out[15]}}), .in4(register_1_q));
  assign not_7_out = ~_16x_out;  // NOT_Gate not_7, 16 bits wide
  ExactlyOne _16x_2[15:0] (.out(_16x_2_out), .in0(ACCUMULATOR), .in3({16{not_2_out[15]}}), .in4({16{not_2_out[15]}}));
  ExactlyOne _16x_3[15:0] (.out(_16x_3_out), .in0({16{not_3_out[15]}}), .in1({16{not_3_out[15]}}), .in4(register_1_q));
  ExactlyOne _16x_4[15:0] (.out(_16x_4_out), .in0(ACCUMULATOR), .in3({16{not_3_out[15]}}), .in4({16{not_3_out[15]}}));
  ExactlyOne _16x_5[15:0] (.out(_16x_5_out), .in0({16{not_4_out[15]}}), .in1({16{not_4_out[15]}}), .in3(ACCUMULATOR));
  ExactlyOne _16x_6[15:0] (.out(_16x_6_out), .in0({16{not_5_out[15]}}), .in1({16{not_5_out[15]}}), .in3(register_1_q));
  ExactlyOne x16[15:0] (.out(x16_out), .in0({16{not_6_out[15]}}), .in1({16{not_6_out[15]}}), .in3(ACCUMULATOR));
  assign _16x_7_out = {16{SUB}} & not_7_out;  // AND_Gate _16x_7, 16 bits wide
  assign _16x_8_out = _16x_7_out | _16x_3_out;  // OR_Gate _16x_8, 16 bits wide
  assign _16x_9_out = _16x_2_out | _16x_4_out;  // OR_Gate _16x_9, 16 bits wide
  Comparator #(.width(16)) comparator_1 (.a(_16x_5_out), .b({16{1'b0}}), .lt(_0));  // open: gt, eq
  Shifter #(.width(16)) shifter_1 (.in(x16_out), .\dist (register_1_q[3:0]), .out(shifter_1_out));
  Adder #(.width(16)) adder_1 (.a(_16x_8_out), .b(_16x_9_out), .out(adder_1_out), .cin(SUB));  // open: cout
  Shifter #(.width(16), .shift("lr")) shifter_2 (.in(shifter_1_out), .\dist (register_1_q[7:4]), .out(shifter_2_out));
  assign OUT = adder_1_out | _16x_6_out | shifter_2_out;  // OR_Gate _16x_10, 16 bits wide
endmodule

module Instruction_Register (
  input  [15:0] MEM,
  input  CLK,
  input  DOOUT,
  input  INSTOUT,
  output [7:0] ADDRESS,
  output [7:0] INSTRUCTION
);

  wire [15:0] Instruction_q;
  wire [15:8] _16x_out;

  Register #(.width(16), .trigger("high")) u_Instruction (
    .D(MEM), .en(1'b1), .Q(Instruction_q), .clk(CLK));  // open: clr
  assign {_16x_out, ADDRESS} = Instruction_q & {{9{1'b1}}, {7{DOOUT}}};  // AND_Gate _16x, 16 bits wide
  assign INSTRUCTION = _16x_out & {8{INSTOUT}};  // AND_Gate and_1, 8 bits wide
endmodule

module Decoder (
  input  INSTOUT,
  input  [7:0] INSTRUCTION,
  output ADD,
  output SUB,
  output JMP,
  output TAC,
  output STO,
  output CLA,
  output OUT,
  output HRS,
  output INP,
  output SFT,
  output GETMEM
);

  wire _0_out, _1_out, _2_out, _3_out, _4_out, _5_out, _6_out, _7_out, _8_out, and_1_out, and_2_out,
       and_3_out, and_4_out, and_5_out, and_6_out, and_7_out, and_8_out, and_9_out, and_10_out, and_11_out,
       not_1_out, not_2_out, not_3_out, not_4_out, not_5_out, not_6_out, not_7_out, not_8_out, xor_1_out;

  not not_1 (not_1_out, INSTRUCTION[4]);
  not not_2 (not_2_out, INSTRUCTION[5]);
  not not_3 (not_3_out, INSTRUCTION[6]);
  not not_4 (not_4_out, INSTRUCTION[7]);
  and and_1 (and_1_out, not_1_out, not_2_out, not_3_out, not_4_out);
  and and_2 (and_2_out, not_1_out, not_2_out, not_3_out, not_4_out);
  and and_3 (and_3_out, not_1_out, not_2_out, not_3_out, not_4_out);
  and and_4 (and_4_out, not_1_out, not_2_out, not_3_out, not_4_out);
  and and_5 (and_5_out, not_1_out, not_2_out, not_3_out, not_4_out);
  and and_6 (and_6_out, not_1_out, not_2_out, not_3_out, not_4_out);
  and and_7 (and_7_out, not_1_out, not_2_out, not_3_out, not_4_out);
  and and_8 (and_8_out, not_1_out, not_2_out, not_3_out, not_4_out);
  and and_9 (and_9_out, not_1_out, not_2_out, not_3_out, not_4_out);
  and and_10 (and_10_out, not_1_out, not_2_out, not_3_out, not_4_out);
  not not_5 (not_5_out, INSTRUCTION[0]);
  not not_6 (not_6_out, INSTRUCTION[1]);
  not not_7 (not_7_out, INSTRUCTION[2]);
  not not_8 (not_8_out, INSTRUCTION[3]);
  and _1 (_1_out, INSTRUCTION[0], not_6_out, not_7_out, not_8_out, and_1_out);
  and _2 (_2_out, not_5_out, INSTRUCTION[1], not_7_out, not_8_out, and_2_out);
  and _3 (_3_out, INSTRUCTION[0], INSTRUCTION[1], not_7_out, not_8_out, and_3_out);
  and _4 (_4_out, not_5_out, not_6_out, INSTRUCTION[2], not_8_out, and_4_out);
  and _5 (_5_out, INSTRUCTION[0], not_6_out, INSTRUCTION[2], not_8_out, and_5_out);
  and _6 (_6_out, not_5_out, INSTRUCTION[1], INSTRUCTION[2], not_8_out, and_6_out);
  and _7 (_7_out, INSTRUCTION[0], INSTRUCTION[1], INSTRUCTION[2], not_8_out, and_7_out);
  and _8 (_8_out, not_5_out, not_6_out, not_7_out, INSTRUCTION[3], and_8_out);
  and _0 (_0_out, not_5_out, not_6_out, not_7_out, not_8_out, and_9_out);
  and and_11 (and_11_out, INSTRUCTION[0], not_6_out, not_7_out, INSTRUCTION[3], and_10_out);
  ExactlyOne xor_1 (
    .out(xor_1_out), .in0(_1_out), .in1(_2_out), .in2(_3_out), .in3(_4_out), .in4(_5_out), .in5(_6_out),
    .in6(_7_out), .in7(_8_out), .in8(_0_out), .in9(and_11_out));
  and and_12 (ADD, xor_1_out, INSTOUT, _1_out);
  and and_13 (SUB, xor_1_out, INSTOUT, _2_out);
  and and_14 (JMP, xor_1_out, INSTOUT, _3_out);
  and and_15 (TAC, xor_1_out, INSTOUT, _4_out);
  and and_16 (STO, xor_1_out, INSTOUT, _5_out);
  and and_17 (CLA, xor_1_out, INSTOUT, _6_out);
  and and_18 (OUT, xor_1_out, INSTOUT, _7_out);
  and and_19 (HRS, xor_1_out, INSTOUT, _8_out);
  and and_20 (INP, xor_1_out, INSTOUT, _0_out);
  and and_21 (SFT, INSTOUT, and_11_out);
  or or_1 (GETMEM, ADD, SUB, JMP, TAC, STO, CLA, OUT, HRS, INP);

  // Notes on the sheet:
  //   NO GETMEM
endmodule

module Clock (
  input  RESUME,
  input  HALT,
  input  PROGMOD,
  output _4,
  output _3,
  output _2,
  output _1,
  output _0
);

  wire and_1_out, and_2_out, CLK_out, not_1_out, not_2_out, not_3_out, not_4_out, not_5_out, or_1_out,
       or_2_out, s_r_ff_1_q, s_r_ff_1_qn, xor_1_out;

  Clock_part CLK (.out(CLK_out));
  xor xor_1 (xor_1_out, RESUME, s_r_ff_1_qn);
  S_R_Flip_Flop s_r_ff_1 (.Q(s_r_ff_1_q), .Qn(s_r_ff_1_qn), .preset(HALT), .reset(RESUME));  // open: S, clk, R, en
  and and_1 (and_1_out, CLK_out, xor_1_out);
  Shift_Register #(.length(5)) shift_register_1 (
    .in(and_2_out), .clk(and_1_out), .clr(or_1_out), .q0(_0), .q1(_1), .q2(_2), .q3(_3), .q4(_4));  // open: shift, out, load, d0, d1, d2, d3, d4
  not not_1 (not_1_out, _1);
  not not_2 (not_2_out, _0);
  not not_3 (not_3_out, _2);
  and and_2 (and_2_out, not_2_out, not_1_out, not_3_out, not_5_out, or_2_out);
  or or_1 (or_1_out, s_r_ff_1_q, PROGMOD);
  not not_4 (not_4_out, _4);
  not not_5 (not_5_out, _3);
  or or_2 (or_2_out, not_4_out, _4);
endmodule

module Address_Bus (
  input  [15:0] Address,
  input  LOAD,
  output [15:0] Address_Out,
  output BUSY
);

  assign Address_Out = Address & {16{LOAD}};  // AND_Gate _16x, 16 bits wide

  assign BUSY = LOAD;
endmodule

module Non_Volatile_Mem___128_B___8_words (
  input  NEXT,
  input  RESETINDEX,
  input  MODE,
  input  [15:0] DATAIN,
  output [15:0] DATAOUT,
  output LINK
);

  wire and_1_out, and_2_out, and_3_out, and_4_out, and_5_out, and_6_out, and_7_out, and_8_out, and_9_out,
       and_10_out, and_19_out, nor_1_out, not_1_out, not_2_out, not_5_out, not_6_out, or_1_out, or_2_out,
       shift_register_2_q0, shift_register_2_q1, xor_1_out;
  wire [15:0] and_11_out, and_12_out, and_13_out, and_14_out, and_15_out, and_16_out, and_17_out, and_18_out,
       not_3_out, or_3_out, register_1_q, register_2_q, register_3_q, register_4_q, register_5_q,
       register_6_q, register_7_q, register_8_q, register_9_q;
  wire [15:15] not_4_out, shift_register_1_q0, shift_register_1_q1, shift_register_1_q2, shift_register_1_q3,
       shift_register_1_q4, shift_register_1_q5, shift_register_1_q6, shift_register_1_q7;

  Register #(.width(16), .trigger("high")) register_1 (.D(DATAIN), .Q(register_1_q), .clk(NEXT));  // open: en, clr
  and and_1 (and_1_out, MODE, NEXT);
  and and_2 (and_2_out, not_6_out, and_1_out, shift_register_1_q0[15]);
  and and_3 (and_3_out, not_6_out, and_1_out, shift_register_1_q1[15]);
  and and_4 (and_4_out, not_6_out, and_1_out, shift_register_1_q2[15]);
  and and_5 (and_5_out, not_6_out, and_1_out, shift_register_1_q3[15]);
  and and_6 (and_6_out, not_6_out, and_1_out, shift_register_1_q4[15]);
  and and_7 (and_7_out, not_6_out, and_1_out, shift_register_1_q5[15]);
  and and_8 (and_8_out, not_6_out, and_1_out, shift_register_1_q6[15]);
  Register #(.width(16), .trigger("high")) register_2 (
    .D(register_1_q), .Q(register_2_q), .clk(and_2_out));  // open: en, clr
  Register #(.width(16), .trigger("high")) register_3 (
    .D(register_1_q), .Q(register_3_q), .clk(and_3_out));  // open: en, clr
  Register #(.width(16), .trigger("high")) register_4 (
    .D(register_1_q), .Q(register_4_q), .clk(and_4_out));  // open: en, clr
  Register #(.width(16), .trigger("high")) register_5 (
    .D(register_1_q), .Q(register_5_q), .clk(and_5_out));  // open: en, clr
  Register #(.width(16), .trigger("high")) register_6 (
    .D(register_1_q), .Q(register_6_q), .clk(and_6_out));  // open: en, clr
  Register #(.width(16), .trigger("high")) register_7 (
    .D(register_1_q), .Q(register_7_q), .clk(and_7_out));  // open: en, clr
  Register #(.width(16), .trigger("high")) register_8 (
    .D(register_1_q), .Q(register_8_q), .clk(and_8_out));  // open: en, clr
  Register #(.width(16), .trigger("high")) register_9 (
    .D(register_1_q), .Q(register_9_q), .clk(and_9_out));  // open: en, clr
  and and_9 (and_9_out, shift_register_1_q7[15], not_6_out, and_1_out);
  not not_1 (not_1_out, not_2_out);
  not not_2 (not_2_out, NEXT);
  or or_1 (or_1_out, shift_register_1_q7[15], nor_1_out);
  and and_10 (and_10_out, NEXT, or_1_out);
  nor nor_1 (nor_1_out, shift_register_1_q0[15], shift_register_1_q1[15], shift_register_1_q2[15], shift_register_1_q3[15], shift_register_1_q4[15], shift_register_1_q5[15], shift_register_1_q6[15], shift_register_1_q7[15]);
  ExactlyOne xor_1 (.out(xor_1_out), .in0(shift_register_2_q0), .in1(shift_register_2_q0), .in2(and_10_out));
  Shift_Register shift_register_1 (
    .in(xor_1_out), .clk(or_2_out), .clr(RESETINDEX), .q0(shift_register_1_q0[15]),
    .q1(shift_register_1_q1[15]), .q2(shift_register_1_q2[15]), .q3(shift_register_1_q3[15]),
    .q4(shift_register_1_q4[15]), .q5(shift_register_1_q5[15]), .q6(shift_register_1_q6[15]),
    .q7(shift_register_1_q7[15]));  // open: shift, out, load, d0, d1, d2, d3, d4, d5, d6, d7
  buf or_2 (or_2_out, not_1_out);  // OR_Gate
  assign not_3_out = ~{16{MODE}};  // NOT_Gate not_3, 16 bits wide
  assign and_11_out = {16{shift_register_1_q0[15]}} & not_3_out & register_2_q;  // AND_Gate and_11, 16 bits wide
  assign and_12_out = {16{shift_register_1_q1[15]}} & not_3_out & register_3_q;  // AND_Gate and_12, 16 bits wide
  assign and_13_out = {16{shift_register_1_q2[15]}} & not_3_out & register_4_q;  // AND_Gate and_13, 16 bits wide
  assign and_14_out = {16{shift_register_1_q3[15]}} & not_3_out & register_5_q;  // AND_Gate and_14, 16 bits wide
  assign and_15_out = {16{shift_register_1_q4[15]}} & not_3_out & register_6_q;  // AND_Gate and_15, 16 bits wide
  assign and_16_out = {16{shift_register_1_q5[15]}} & not_3_out & register_7_q;  // AND_Gate and_16, 16 bits wide
  assign and_17_out = {16{shift_register_1_q6[15]}} & not_3_out & register_8_q;  // AND_Gate and_17, 16 bits wide
  assign and_18_out = {16{shift_register_1_q7[15]}} & not_3_out & register_9_q;  // AND_Gate and_18, 16 bits wide
  and and_19 (and_19_out, shift_register_1_q7[15], not_1_out);
  Shift_Register #(.length(2)) shift_register_2 (
    .shift(not_5_out), .in(shift_register_1_q7[15]), .clk(and_19_out), .clr(RESETINDEX),
    .q0(shift_register_2_q0), .q1(shift_register_2_q1));  // open: out, load, d0, d1
  not not_4 (not_4_out[15], shift_register_2_q1);
  not not_5 (not_5_out, shift_register_2_q1);
  not not_6 (not_6_out, shift_register_2_q1);
  assign or_3_out = and_11_out | and_12_out | and_13_out | and_14_out | and_15_out | and_16_out | and_17_out | and_18_out;  // OR_Gate or_3, 16 bits wide
  assign DATAOUT = or_3_out & {16{not_4_out[15]}};  // AND_Gate and_20, 16 bits wide
  and and_21 (LINK, shift_register_2_q1, not_1_out);

  // Notes on the sheet:
  //   0 = READ
  //   1 = WRITE
endmodule

module Non_Volatile_Mem___2_KB___128_words (
  input  NEXT,
  input  RESETINDEX,
  input  MODE,
  input  [15:0] DATAIN,
  output [15:0] DATAOUT,
  output LINK
);

  wire non_volatile_mem_128_b_8_words_1_link, non_volatile_mem_128_b_8_words_2_link,
       non_volatile_mem_128_b_8_words_3_link, non_volatile_mem_128_b_8_words_4_link,
       non_volatile_mem_128_b_8_words_5_link, non_volatile_mem_128_b_8_words_6_link,
       non_volatile_mem_128_b_8_words_7_link, non_volatile_mem_128_b_8_words_8_link,
       non_volatile_mem_128_b_8_words_9_link, non_volatile_mem_128_b_8_words_10_link,
       non_volatile_mem_128_b_8_words_11_link, non_volatile_mem_128_b_8_words_12_link,
       non_volatile_mem_128_b_8_words_13_link, non_volatile_mem_128_b_8_words_14_link,
       non_volatile_mem_128_b_8_words_15_link;
  wire [15:0] non_volatile_mem_128_b_8_words_1_dataout, non_volatile_mem_128_b_8_words_2_dataout,
       non_volatile_mem_128_b_8_words_3_dataout, non_volatile_mem_128_b_8_words_4_dataout,
       non_volatile_mem_128_b_8_words_5_dataout, non_volatile_mem_128_b_8_words_6_dataout,
       non_volatile_mem_128_b_8_words_7_dataout, non_volatile_mem_128_b_8_words_8_dataout,
       non_volatile_mem_128_b_8_words_9_dataout, non_volatile_mem_128_b_8_words_10_dataout,
       non_volatile_mem_128_b_8_words_11_dataout, non_volatile_mem_128_b_8_words_12_dataout,
       non_volatile_mem_128_b_8_words_13_dataout, non_volatile_mem_128_b_8_words_14_dataout,
       non_volatile_mem_128_b_8_words_15_dataout, non_volatile_mem_128_b_8_words_16_dataout, or_1_out,
       or_2_out, or_3_out, or_4_out;

  Non_Volatile_Mem___128_B___8_words non_volatile_mem_128_b_8_words_1 (
    .NEXT(NEXT), .RESETINDEX(RESETINDEX), .MODE(MODE), .DATAIN(DATAIN),
    .DATAOUT(non_volatile_mem_128_b_8_words_1_dataout), .LINK(non_volatile_mem_128_b_8_words_1_link));
  Non_Volatile_Mem___128_B___8_words non_volatile_mem_128_b_8_words_2 (
    .NEXT(non_volatile_mem_128_b_8_words_1_link), .RESETINDEX(RESETINDEX), .MODE(MODE), .DATAIN(DATAIN),
    .DATAOUT(non_volatile_mem_128_b_8_words_2_dataout), .LINK(non_volatile_mem_128_b_8_words_2_link));
  Non_Volatile_Mem___128_B___8_words non_volatile_mem_128_b_8_words_3 (
    .NEXT(non_volatile_mem_128_b_8_words_2_link), .RESETINDEX(RESETINDEX), .MODE(MODE), .DATAIN(DATAIN),
    .DATAOUT(non_volatile_mem_128_b_8_words_3_dataout), .LINK(non_volatile_mem_128_b_8_words_3_link));
  Non_Volatile_Mem___128_B___8_words non_volatile_mem_128_b_8_words_4 (
    .NEXT(non_volatile_mem_128_b_8_words_3_link), .RESETINDEX(RESETINDEX), .MODE(MODE), .DATAIN(DATAIN),
    .DATAOUT(non_volatile_mem_128_b_8_words_4_dataout), .LINK(non_volatile_mem_128_b_8_words_4_link));
  Non_Volatile_Mem___128_B___8_words non_volatile_mem_128_b_8_words_5 (
    .NEXT(non_volatile_mem_128_b_8_words_4_link), .RESETINDEX(RESETINDEX), .MODE(MODE), .DATAIN(DATAIN),
    .DATAOUT(non_volatile_mem_128_b_8_words_5_dataout), .LINK(non_volatile_mem_128_b_8_words_5_link));
  Non_Volatile_Mem___128_B___8_words non_volatile_mem_128_b_8_words_6 (
    .NEXT(non_volatile_mem_128_b_8_words_5_link), .RESETINDEX(RESETINDEX), .MODE(MODE), .DATAIN(DATAIN),
    .DATAOUT(non_volatile_mem_128_b_8_words_6_dataout), .LINK(non_volatile_mem_128_b_8_words_6_link));
  Non_Volatile_Mem___128_B___8_words non_volatile_mem_128_b_8_words_7 (
    .NEXT(non_volatile_mem_128_b_8_words_6_link), .RESETINDEX(RESETINDEX), .MODE(MODE), .DATAIN(DATAIN),
    .DATAOUT(non_volatile_mem_128_b_8_words_7_dataout), .LINK(non_volatile_mem_128_b_8_words_7_link));
  Non_Volatile_Mem___128_B___8_words non_volatile_mem_128_b_8_words_8 (
    .NEXT(non_volatile_mem_128_b_8_words_7_link), .RESETINDEX(RESETINDEX), .MODE(MODE), .DATAIN(DATAIN),
    .DATAOUT(non_volatile_mem_128_b_8_words_8_dataout), .LINK(non_volatile_mem_128_b_8_words_8_link));
  Non_Volatile_Mem___128_B___8_words non_volatile_mem_128_b_8_words_9 (
    .NEXT(non_volatile_mem_128_b_8_words_8_link), .RESETINDEX(RESETINDEX), .MODE(MODE), .DATAIN(DATAIN),
    .DATAOUT(non_volatile_mem_128_b_8_words_9_dataout), .LINK(non_volatile_mem_128_b_8_words_9_link));
  Non_Volatile_Mem___128_B___8_words non_volatile_mem_128_b_8_words_10 (
    .NEXT(non_volatile_mem_128_b_8_words_9_link), .RESETINDEX(RESETINDEX), .MODE(MODE), .DATAIN(DATAIN),
    .DATAOUT(non_volatile_mem_128_b_8_words_10_dataout), .LINK(non_volatile_mem_128_b_8_words_10_link));
  Non_Volatile_Mem___128_B___8_words non_volatile_mem_128_b_8_words_11 (
    .NEXT(non_volatile_mem_128_b_8_words_10_link), .RESETINDEX(RESETINDEX), .MODE(MODE), .DATAIN(DATAIN),
    .DATAOUT(non_volatile_mem_128_b_8_words_11_dataout), .LINK(non_volatile_mem_128_b_8_words_11_link));
  Non_Volatile_Mem___128_B___8_words non_volatile_mem_128_b_8_words_12 (
    .NEXT(non_volatile_mem_128_b_8_words_11_link), .RESETINDEX(RESETINDEX), .MODE(MODE), .DATAIN(DATAIN),
    .DATAOUT(non_volatile_mem_128_b_8_words_12_dataout), .LINK(non_volatile_mem_128_b_8_words_12_link));
  Non_Volatile_Mem___128_B___8_words non_volatile_mem_128_b_8_words_13 (
    .NEXT(non_volatile_mem_128_b_8_words_12_link), .RESETINDEX(RESETINDEX), .MODE(MODE), .DATAIN(DATAIN),
    .DATAOUT(non_volatile_mem_128_b_8_words_13_dataout), .LINK(non_volatile_mem_128_b_8_words_13_link));
  Non_Volatile_Mem___128_B___8_words non_volatile_mem_128_b_8_words_14 (
    .NEXT(non_volatile_mem_128_b_8_words_13_link), .RESETINDEX(RESETINDEX), .MODE(MODE), .DATAIN(DATAIN),
    .DATAOUT(non_volatile_mem_128_b_8_words_14_dataout), .LINK(non_volatile_mem_128_b_8_words_14_link));
  Non_Volatile_Mem___128_B___8_words non_volatile_mem_128_b_8_words_15 (
    .NEXT(non_volatile_mem_128_b_8_words_14_link), .RESETINDEX(RESETINDEX), .MODE(MODE), .DATAIN(DATAIN),
    .DATAOUT(non_volatile_mem_128_b_8_words_15_dataout), .LINK(non_volatile_mem_128_b_8_words_15_link));
  Non_Volatile_Mem___128_B___8_words non_volatile_mem_128_b_8_words_16 (
    .NEXT(non_volatile_mem_128_b_8_words_15_link), .RESETINDEX(RESETINDEX), .MODE(MODE), .DATAIN(DATAIN),
    .DATAOUT(non_volatile_mem_128_b_8_words_16_dataout), .LINK(LINK));
  assign or_1_out = non_volatile_mem_128_b_8_words_13_dataout | non_volatile_mem_128_b_8_words_9_dataout | non_volatile_mem_128_b_8_words_5_dataout | non_volatile_mem_128_b_8_words_1_dataout;  // OR_Gate or_1, 16 bits wide
  assign or_2_out = non_volatile_mem_128_b_8_words_14_dataout | non_volatile_mem_128_b_8_words_10_dataout | non_volatile_mem_128_b_8_words_6_dataout | non_volatile_mem_128_b_8_words_2_dataout;  // OR_Gate or_2, 16 bits wide
  assign or_3_out = non_volatile_mem_128_b_8_words_15_dataout | non_volatile_mem_128_b_8_words_11_dataout | non_volatile_mem_128_b_8_words_7_dataout | non_volatile_mem_128_b_8_words_3_dataout;  // OR_Gate or_3, 16 bits wide
  assign or_4_out = non_volatile_mem_128_b_8_words_16_dataout | non_volatile_mem_128_b_8_words_12_dataout | non_volatile_mem_128_b_8_words_8_dataout | non_volatile_mem_128_b_8_words_4_dataout;  // OR_Gate or_4, 16 bits wide
  assign DATAOUT = or_1_out | or_2_out | or_3_out | or_4_out;  // OR_Gate or_5, 16 bits wide
endmodule

module Non_Volatile_Mem___32_KB___2048_words (
  input  NEXT,
  input  RESETINDEX,
  input  MODE,
  input  [15:0] DATAIN,
  output [15:0] DATAOUT,
  output LINK
);

  wire non_volatile_mem_2_kb_128_words_1_link, non_volatile_mem_2_kb_128_words_2_link,
       non_volatile_mem_2_kb_128_words_3_link, non_volatile_mem_2_kb_128_words_4_link,
       non_volatile_mem_2_kb_128_words_5_link, non_volatile_mem_2_kb_128_words_6_link,
       non_volatile_mem_2_kb_128_words_7_link, non_volatile_mem_2_kb_128_words_8_link,
       non_volatile_mem_2_kb_128_words_9_link, non_volatile_mem_2_kb_128_words_10_link,
       non_volatile_mem_2_kb_128_words_11_link, non_volatile_mem_2_kb_128_words_12_link,
       non_volatile_mem_2_kb_128_words_13_link, non_volatile_mem_2_kb_128_words_14_link,
       non_volatile_mem_2_kb_128_words_15_link;
  wire [15:0] non_volatile_mem_2_kb_128_words_1_dataout, non_volatile_mem_2_kb_128_words_2_dataout,
       non_volatile_mem_2_kb_128_words_3_dataout, non_volatile_mem_2_kb_128_words_4_dataout,
       non_volatile_mem_2_kb_128_words_5_dataout, non_volatile_mem_2_kb_128_words_6_dataout,
       non_volatile_mem_2_kb_128_words_7_dataout, non_volatile_mem_2_kb_128_words_8_dataout,
       non_volatile_mem_2_kb_128_words_9_dataout, non_volatile_mem_2_kb_128_words_10_dataout,
       non_volatile_mem_2_kb_128_words_11_dataout, non_volatile_mem_2_kb_128_words_12_dataout,
       non_volatile_mem_2_kb_128_words_13_dataout, non_volatile_mem_2_kb_128_words_14_dataout,
       non_volatile_mem_2_kb_128_words_15_dataout, non_volatile_mem_2_kb_128_words_16_dataout, or_1_out,
       or_2_out, or_3_out, or_4_out;

  Non_Volatile_Mem___2_KB___128_words non_volatile_mem_2_kb_128_words_1 (
    .NEXT(NEXT), .RESETINDEX(RESETINDEX), .MODE(MODE), .DATAIN(DATAIN),
    .DATAOUT(non_volatile_mem_2_kb_128_words_1_dataout), .LINK(non_volatile_mem_2_kb_128_words_1_link));
  Non_Volatile_Mem___2_KB___128_words non_volatile_mem_2_kb_128_words_2 (
    .NEXT(non_volatile_mem_2_kb_128_words_1_link), .RESETINDEX(RESETINDEX), .MODE(MODE), .DATAIN(DATAIN),
    .DATAOUT(non_volatile_mem_2_kb_128_words_2_dataout), .LINK(non_volatile_mem_2_kb_128_words_2_link));
  Non_Volatile_Mem___2_KB___128_words non_volatile_mem_2_kb_128_words_3 (
    .NEXT(non_volatile_mem_2_kb_128_words_2_link), .RESETINDEX(RESETINDEX), .MODE(MODE), .DATAIN(DATAIN),
    .DATAOUT(non_volatile_mem_2_kb_128_words_3_dataout), .LINK(non_volatile_mem_2_kb_128_words_3_link));
  Non_Volatile_Mem___2_KB___128_words non_volatile_mem_2_kb_128_words_4 (
    .NEXT(non_volatile_mem_2_kb_128_words_3_link), .RESETINDEX(RESETINDEX), .MODE(MODE), .DATAIN(DATAIN),
    .DATAOUT(non_volatile_mem_2_kb_128_words_4_dataout), .LINK(non_volatile_mem_2_kb_128_words_4_link));
  Non_Volatile_Mem___2_KB___128_words non_volatile_mem_2_kb_128_words_5 (
    .NEXT(non_volatile_mem_2_kb_128_words_4_link), .RESETINDEX(RESETINDEX), .MODE(MODE), .DATAIN(DATAIN),
    .DATAOUT(non_volatile_mem_2_kb_128_words_5_dataout), .LINK(non_volatile_mem_2_kb_128_words_5_link));
  Non_Volatile_Mem___2_KB___128_words non_volatile_mem_2_kb_128_words_6 (
    .NEXT(non_volatile_mem_2_kb_128_words_5_link), .RESETINDEX(RESETINDEX), .MODE(MODE), .DATAIN(DATAIN),
    .DATAOUT(non_volatile_mem_2_kb_128_words_6_dataout), .LINK(non_volatile_mem_2_kb_128_words_6_link));
  Non_Volatile_Mem___2_KB___128_words non_volatile_mem_2_kb_128_words_7 (
    .NEXT(non_volatile_mem_2_kb_128_words_6_link), .RESETINDEX(RESETINDEX), .MODE(MODE), .DATAIN(DATAIN),
    .DATAOUT(non_volatile_mem_2_kb_128_words_7_dataout), .LINK(non_volatile_mem_2_kb_128_words_7_link));
  Non_Volatile_Mem___2_KB___128_words non_volatile_mem_2_kb_128_words_8 (
    .NEXT(non_volatile_mem_2_kb_128_words_7_link), .RESETINDEX(RESETINDEX), .MODE(MODE), .DATAIN(DATAIN),
    .DATAOUT(non_volatile_mem_2_kb_128_words_8_dataout), .LINK(non_volatile_mem_2_kb_128_words_8_link));
  Non_Volatile_Mem___2_KB___128_words non_volatile_mem_2_kb_128_words_9 (
    .NEXT(non_volatile_mem_2_kb_128_words_8_link), .RESETINDEX(RESETINDEX), .MODE(MODE), .DATAIN(DATAIN),
    .DATAOUT(non_volatile_mem_2_kb_128_words_9_dataout), .LINK(non_volatile_mem_2_kb_128_words_9_link));
  Non_Volatile_Mem___2_KB___128_words non_volatile_mem_2_kb_128_words_10 (
    .NEXT(non_volatile_mem_2_kb_128_words_9_link), .RESETINDEX(RESETINDEX), .MODE(MODE), .DATAIN(DATAIN),
    .DATAOUT(non_volatile_mem_2_kb_128_words_10_dataout), .LINK(non_volatile_mem_2_kb_128_words_10_link));
  Non_Volatile_Mem___2_KB___128_words non_volatile_mem_2_kb_128_words_11 (
    .NEXT(non_volatile_mem_2_kb_128_words_10_link), .RESETINDEX(RESETINDEX), .MODE(MODE), .DATAIN(DATAIN),
    .DATAOUT(non_volatile_mem_2_kb_128_words_11_dataout), .LINK(non_volatile_mem_2_kb_128_words_11_link));
  Non_Volatile_Mem___2_KB___128_words non_volatile_mem_2_kb_128_words_12 (
    .NEXT(non_volatile_mem_2_kb_128_words_11_link), .RESETINDEX(RESETINDEX), .MODE(MODE), .DATAIN(DATAIN),
    .DATAOUT(non_volatile_mem_2_kb_128_words_12_dataout), .LINK(non_volatile_mem_2_kb_128_words_12_link));
  Non_Volatile_Mem___2_KB___128_words non_volatile_mem_2_kb_128_words_13 (
    .NEXT(non_volatile_mem_2_kb_128_words_12_link), .RESETINDEX(RESETINDEX), .MODE(MODE), .DATAIN(DATAIN),
    .DATAOUT(non_volatile_mem_2_kb_128_words_13_dataout), .LINK(non_volatile_mem_2_kb_128_words_13_link));
  Non_Volatile_Mem___2_KB___128_words non_volatile_mem_2_kb_128_words_14 (
    .NEXT(non_volatile_mem_2_kb_128_words_13_link), .RESETINDEX(RESETINDEX), .MODE(MODE), .DATAIN(DATAIN),
    .DATAOUT(non_volatile_mem_2_kb_128_words_14_dataout), .LINK(non_volatile_mem_2_kb_128_words_14_link));
  Non_Volatile_Mem___2_KB___128_words non_volatile_mem_2_kb_128_words_15 (
    .NEXT(non_volatile_mem_2_kb_128_words_14_link), .RESETINDEX(RESETINDEX), .MODE(MODE), .DATAIN(DATAIN),
    .DATAOUT(non_volatile_mem_2_kb_128_words_15_dataout), .LINK(non_volatile_mem_2_kb_128_words_15_link));
  Non_Volatile_Mem___2_KB___128_words non_volatile_mem_2_kb_128_words_16 (
    .NEXT(non_volatile_mem_2_kb_128_words_15_link), .RESETINDEX(RESETINDEX), .MODE(MODE), .DATAIN(DATAIN),
    .DATAOUT(non_volatile_mem_2_kb_128_words_16_dataout), .LINK(LINK));
  assign or_1_out = non_volatile_mem_2_kb_128_words_13_dataout | non_volatile_mem_2_kb_128_words_9_dataout | non_volatile_mem_2_kb_128_words_5_dataout | non_volatile_mem_2_kb_128_words_1_dataout;  // OR_Gate or_1, 16 bits wide
  assign or_2_out = non_volatile_mem_2_kb_128_words_14_dataout | non_volatile_mem_2_kb_128_words_10_dataout | non_volatile_mem_2_kb_128_words_6_dataout | non_volatile_mem_2_kb_128_words_2_dataout;  // OR_Gate or_2, 16 bits wide
  assign or_3_out = non_volatile_mem_2_kb_128_words_15_dataout | non_volatile_mem_2_kb_128_words_11_dataout | non_volatile_mem_2_kb_128_words_7_dataout | non_volatile_mem_2_kb_128_words_3_dataout;  // OR_Gate or_3, 16 bits wide
  assign or_4_out = non_volatile_mem_2_kb_128_words_16_dataout | non_volatile_mem_2_kb_128_words_12_dataout | non_volatile_mem_2_kb_128_words_8_dataout | non_volatile_mem_2_kb_128_words_4_dataout;  // OR_Gate or_4, 16 bits wide
  assign DATAOUT = or_1_out | or_2_out | or_3_out | or_4_out;  // OR_Gate or_5, 16 bits wide
endmodule

module NV_Mem_Loader_Addresser___4_KB___256_words (
  input  MODE,
  input  NEXT,
  input  RESETINDEX,
  output [15:0] DATAOUT
);

  wire and_1_out, button_1_out, clock_1_out, d_ff_1_q, non_volatile_mem_2_kb_128_words_1_link,
       non_volatile_mem_2_kb_128_words_2_link, or_1_out, or_2_out, or_3_out, or_4_out;
  wire [7:0] program_counter_1_out, subtractor_1_out;
  wire [15:0] non_volatile_mem_2_kb_128_words_1_dataout, non_volatile_mem_2_kb_128_words_2_dataout,
       ram_1_data;

  D_Flip_Flop d_ff_1 (
    .Q(d_ff_1_q), .preset(button_1_out), .reset(non_volatile_mem_2_kb_128_words_2_link));  // open: clk, D, Qn, en
  Button button_1 (.out(button_1_out));
  Clock_part clock_1 (.out(clock_1_out));
  and and_1 (and_1_out, d_ff_1_q, clock_1_out);
  or or_1 (or_1_out, and_1_out, NEXT);
  or or_2 (or_2_out, RESETINDEX, non_volatile_mem_2_kb_128_words_2_link);
  Program_Counter program_counter_1 (
    .JUMP(1'b0), .CLEAR(non_volatile_mem_2_kb_128_words_2_link), .OUT(program_counter_1_out),
    .LOAD(or_1_out), .CLK(or_1_out));  // open: ADDR1
  or or_3 (or_3_out, or_1_out, NEXT);
  or or_4 (or_4_out, or_1_out, NEXT);
  Subtractor subtractor_1 (.a(program_counter_1_out), .b(8'h1), .out(subtractor_1_out));  // open: bin, bout
  RAM #(.dataWidth(16)) ram_1 (
    .addr(subtractor_1_out), .data(ram_1_data), .sel(1'b1), .ld(or_4_out));  // open: clk, clr
  Non_Volatile_Mem___2_KB___128_words non_volatile_mem_2_kb_128_words_1 (
    .NEXT(or_3_out), .RESETINDEX(or_2_out), .MODE(MODE), .DATAIN(ram_1_data),
    .DATAOUT(non_volatile_mem_2_kb_128_words_1_dataout), .LINK(non_volatile_mem_2_kb_128_words_1_link));
  Non_Volatile_Mem___2_KB___128_words non_volatile_mem_2_kb_128_words_2 (
    .NEXT(non_volatile_mem_2_kb_128_words_1_link), .RESETINDEX(or_2_out), .MODE(MODE), .DATAIN(ram_1_data),
    .DATAOUT(non_volatile_mem_2_kb_128_words_2_dataout), .LINK(non_volatile_mem_2_kb_128_words_2_link));
  assign DATAOUT = non_volatile_mem_2_kb_128_words_1_dataout | non_volatile_mem_2_kb_128_words_2_dataout;  // OR_Gate or_5, 16 bits wide
endmodule
